// Logisim project proj_3.circ as structural Verilog: 4 circuits, main circuit main
module main (
  input  x
);

  wire base6_updown_counter_1__1, base6_updown_counter_1__2, base6_updown_counter_1__4, clock_1_out,
       dec_7seg_driver_1_a, dec_7seg_driver_1_b, dec_7seg_driver_1_c, dec_7seg_driver_1_d,
       dec_7seg_driver_1_e, dec_7seg_driver_1_f, dec_7seg_driver_1_g, dec_7seg_driver_2_a,
       dec_7seg_driver_2_b, dec_7seg_driver_2_c, dec_7seg_driver_2_d, dec_7seg_driver_2_e,
       dec_7seg_driver_2_f, dec_7seg_driver_2_g, dec_updown_counter_1__1, dec_updown_counter_1__2,
       dec_updown_counter_1__4, dec_updown_counter_1__8, dec_updown_counter_1_carry;

  base6_updown_counter base6_updown_counter_1 (
    .X(x), .Clock(dec_updown_counter_1_carry), ._1(base6_updown_counter_1__1),
    ._2(base6_updown_counter_1__2), ._4(base6_updown_counter_1__4));
  dec_updown_counter dec_updown_counter_1 (
    .X(x), .Carry(dec_updown_counter_1_carry), .Clock(clock_1_out), ._1(dec_updown_counter_1__1),
    ._2(dec_updown_counter_1__2), ._4(dec_updown_counter_1__4), ._8(dec_updown_counter_1__8));
  Clock clock_1 (.out(clock_1_out));
  dec_7seg_driver dec_7seg_driver_1 (
    .w(base6_updown_counter_1__1), .x(base6_updown_counter_1__2), .y(base6_updown_counter_1__4), .z(1'b0),
    .b(dec_7seg_driver_1_b), .a(dec_7seg_driver_1_a), .f(dec_7seg_driver_1_f), .g(dec_7seg_driver_1_g),
    .e(dec_7seg_driver_1_e), .d(dec_7seg_driver_1_d), .c(dec_7seg_driver_1_c));
  dec_7seg_driver dec_7seg_driver_2 (
    .w(dec_updown_counter_1__1), .x(dec_updown_counter_1__2), .y(dec_updown_counter_1__4),
    .z(dec_updown_counter_1__8), .b(dec_7seg_driver_2_b), .a(dec_7seg_driver_2_a), .f(dec_7seg_driver_2_f),
    .g(dec_7seg_driver_2_g), .e(dec_7seg_driver_2_e), .d(dec_7seg_driver_2_d), .c(dec_7seg_driver_2_c));
  _7_Segment_Display u_7_segment_display_1 (
    .g(dec_7seg_driver_1_g), .f(dec_7seg_driver_1_f), .a(dec_7seg_driver_1_a), .b(dec_7seg_driver_1_b),
    .e(dec_7seg_driver_1_e), .d(dec_7seg_driver_1_d), .c(dec_7seg_driver_1_c));  // open: dp
  _7_Segment_Display u_7_segment_display_2 (
    .g(dec_7seg_driver_2_g), .f(dec_7seg_driver_2_f), .a(dec_7seg_driver_2_a), .b(dec_7seg_driver_2_b),
    .e(dec_7seg_driver_2_e), .d(dec_7seg_driver_2_d), .c(dec_7seg_driver_2_c));  // open: dp
endmodule

module dec_7seg_driver (
  input  w,
  input  x,
  input  y,
  input  z,
  output b,
  output a,
  output f,
  output g,
  output e,
  output d,
  output c
);

  wire and_1_out, and_2_out, and_3_out, and_4_out, and_5_out, and_6_out, and_7_out, and_8_out, and_9_out,
       and_10_out, and_11_out, and_12_out, and_13_out, and_14_out, and_15_out, and_16_out, not_1_out,
       not_2_out, not_3_out;

  not not_1 (not_1_out, w);
  not not_2 (not_2_out, x);
  not not_3 (not_3_out, y);
  and and_1 (and_1_out, not_1_out, not_2_out);
  and and_2 (and_2_out, w, x);
  and and_3 (and_3_out, not_1_out, not_3_out);
  and and_4 (and_4_out, w, y);
  and and_5 (and_5_out, not_1_out, not_2_out);
  and and_6 (and_6_out, not_2_out, y);
  and and_7 (and_7_out, not_1_out, y);
  and and_8 (and_8_out, not_3_out, x);
  and and_9 (and_9_out, not_1_out, y);
  and and_10 (and_10_out, not_2_out, y);
  and and_11 (and_11_out, not_1_out, not_3_out);
  and and_12 (and_12_out, not_1_out, x);
  and and_13 (and_13_out, not_1_out, not_3_out);
  and and_14 (and_14_out, w, not_2_out, y);
  and and_15 (and_15_out, not_3_out, x);
  and and_16 (and_16_out, x, not_1_out);
  or or_1 (c, w, not_2_out, y);
  or or_2 (b, and_1_out, not_3_out, and_2_out);
  or or_3 (a, and_3_out, x, z, and_4_out);
  or or_4 (f, and_5_out, and_6_out, and_7_out, z);
  or or_5 (g, and_8_out, and_9_out, and_10_out, z);
  or or_6 (e, and_11_out, and_12_out);
  or or_7 (d, and_13_out, and_14_out, z, and_15_out, and_16_out);
endmodule

module dec_updown_counter (
  input  X,
  input  Clock,
  output Carry,
  output _1,
  output _2,
  output _4,
  output _8
);

  wire and_1_out, and_2_out, and_3_out, and_4_out, and_5_out, and_6_out, and_7_out, and_8_out, j_k_ff_1_qn,
       j_k_ff_2_qn, j_k_ff_3_qn, not_1_out, or_1_out, or_2_out, or_3_out, or_4_out, or_5_out;

  not not_1 (not_1_out, X);
  and and_1 (and_1_out, _1, not_1_out);
  and and_2 (and_2_out, X, j_k_ff_1_qn);
  and and_3 (and_3_out, _2, and_1_out);
  and and_4 (and_4_out, and_2_out, j_k_ff_2_qn);
  and and_5 (and_5_out, _4, and_3_out);
  and and_6 (and_6_out, and_4_out, j_k_ff_3_qn);
  or or_1 (or_1_out, and_1_out, and_2_out);
  or or_2 (or_2_out, and_3_out, and_4_out);
  or or_3 (or_3_out, and_5_out, and_6_out);
  J_K_Flip_Flop j_k_ff_1 (
    .J(Clock), .clk(Clock), .K(Clock), .Q(_1), .Qn(j_k_ff_1_qn), .reset(and_7_out));  // open: preset, en
  J_K_Flip_Flop j_k_ff_2 (
    .J(or_1_out), .clk(Clock), .K(or_1_out), .Q(_2), .Qn(j_k_ff_2_qn), .reset(or_4_out));  // open: preset, en
  or or_4 (or_4_out, and_8_out, and_7_out);
  J_K_Flip_Flop j_k_ff_3 (
    .J(or_2_out), .clk(Clock), .K(or_2_out), .Q(_4), .Qn(j_k_ff_3_qn), .reset(or_5_out));  // open: preset, en
  or or_5 (or_5_out, and_8_out, and_7_out);
  J_K_Flip_Flop j_k_ff_4 (.J(or_3_out), .clk(Clock), .K(or_3_out), .Q(_8), .reset(and_7_out));  // open: Qn, preset, en
  and and_7 (and_7_out, _8, _2, not_1_out);
  and and_8 (and_8_out, _8, _4, _2, _1, X);
  or or_6 (Carry, and_7_out, and_8_out);
endmodule

module base6_updown_counter (
  input  X,
  input  Clock,
  output _1,
  output _2,
  output _4
);

  wire and_1_out, and_2_out, and_3_out, and_4_out, and_5_out, and_6_out, j_k_ff_1_qn, j_k_ff_2_qn,
       j_k_ff_3_qn, not_1_out, or_1_out, or_2_out, or_3_out;

  not not_1 (not_1_out, X);
  and and_1 (and_1_out, _1, not_1_out);
  and and_2 (and_2_out, X, j_k_ff_1_qn);
  and and_3 (and_3_out, _2, and_1_out);
  and and_4 (and_4_out, and_2_out, j_k_ff_2_qn);
  or or_1 (or_1_out, and_1_out, and_2_out);
  or or_2 (or_2_out, and_3_out, and_4_out);
  J_K_Flip_Flop j_k_ff_1 (
    .J(Clock), .clk(Clock), .K(Clock), .Q(_1), .Qn(j_k_ff_1_qn), .reset(and_5_out));  // open: preset, en
  J_K_Flip_Flop j_k_ff_2 (
    .J(or_1_out), .clk(Clock), .K(or_1_out), .Q(_2), .Qn(j_k_ff_2_qn), .reset(or_3_out));  // open: preset, en
  J_K_Flip_Flop j_k_ff_3 (
    .J(or_2_out), .clk(Clock), .K(or_2_out), .Q(_4), .Qn(j_k_ff_3_qn), .reset(and_5_out));  // open: preset, en
  or or_3 (or_3_out, and_6_out, and_5_out);
  and and_5 (and_5_out, _4, _2, not_1_out);
  and and_6 (and_6_out, j_k_ff_3_qn, j_k_ff_2_qn, j_k_ff_1_qn, X);
endmodule
